// Digital circuit part_a.dig as structural Verilog
module part_a (
  input  in_0,
  input  in_1,
  input  in_2,
  output out_0
);

  wire and_1_out, and_2_out, and_3_out, and_4_out, and_5_out, and_6_out, not_1_out, not_2_out, not_3_out;

  not not_1 (not_1_out, in_0);
  not not_2 (not_2_out, in_1);
  not not_3 (not_3_out, in_2);
  and and_1 (and_1_out, not_3_out, not_2_out, not_1_out);
  and and_2 (and_2_out, not_1_out, not_2_out, in_2);
  and and_3 (and_3_out, not_1_out, in_1, not_3_out);
  and and_4 (and_4_out, in_0, not_2_out, not_3_out);
  and and_5 (and_5_out, in_0, not_2_out, in_2);
  and and_6 (and_6_out, in_0, in_1, in_2);
  or or_1 (out_0, and_1_out, and_2_out, and_3_out, and_4_out, and_5_out, and_6_out);
endmodule

/* Test case part_a_test:
in_0 in_1 in_2 out_0
  0    0    0    1
  0    0    1    1
  0    1    0    1
  0    1    1    0
  1    0    0    1
  1    0    1    1
  1    1    0    0
  1    1    1    1
*/
