// Digital circuit part_c.dig as structural Verilog
module part_c (
  input  in_2,
  input  in_0,
  input  in_1,
  output out_0
);

  wire n0_s, n1_s, n4_d, p0_d, p3_d, p4_d, p7_d;

  FGPFET p0 (.G(in_0), .S(1'b1), .D(p0_d));
  FGPFET p1 (.G(in_1), .S(1'b1), .D(p0_d));
  FGNFET n0 (.G(in_0), .D(p0_d), .S(n0_s));
  FGNFET n1 (.G(in_1), .D(n0_s), .S(n1_s));
  FGNFET n2 (.G(in_2), .D(n1_s), .S(1'b0));
  FGPFET p2 (.G(in_2), .S(1'b1), .D(p0_d));
  FGPFET p3 (.G(in_2), .S(1'b1), .D(p3_d));
  FGNFET n3 (.G(in_2), .D(p3_d), .S(1'b0));
  FGPFET p7 (.G(p0_d), .S(1'b1), .D(p7_d));
  FGNFET n7 (.G(p0_d), .D(p7_d), .S(1'b0));
  FGNFET n4 (.G(p3_d), .D(n4_d), .S(1'b0));
  FGPFET p4 (.G(p7_d), .S(1'b1), .D(p4_d));
  FGPFET p5 (.G(p3_d), .S(p4_d), .D(n4_d));
  FGNFET n5 (.G(p7_d), .D(n4_d), .S(1'b0));
  FGPFET p6 (.G(n4_d), .S(1'b1), .D(out_0));
  FGNFET n6 (.G(n4_d), .D(out_0), .S(1'b0));
endmodule

/* Test case part_c_test:
in_0 in_1 in_2 out_0
  0    0    0    1
  0    0    1    0
  0    1    0    1
  0    1    1    0
  1    0    0    1
  1    0    1    0
  1    1    0    1
  1    1    1    1
*/
